// Digital circuit QT Sandbox.dig as structural Verilog
module QT_Sandbox (
  input  clk,
  input  [7:0] Input
);

  wire qtc_1_p6, qtc_1_p8, qtc_1_p9, rs_ff_1_q, rs_ff_as_1_q, Send_out, Turn_On_out;
  wire [7:0] d_ff_1_q, Out_q, qtc_1_p7, register_1_q;

  Button Turn_On (.out(Turn_On_out));
  Button Send (.out(Send_out));
  RS_FF_AS rs_ff_as_1 (.S(Send_out), .R(rs_ff_1_q), .Q(rs_ff_as_1_q));  // open: nQ
  D_FF #(.Bits(8)) d_ff_1 (.D(Input), .C(Send_out), .Q(d_ff_1_q));  // open: nQ
  RS_FF rs_ff_1 (.S(rs_ff_as_1_q), .C(clk), .R(qtc_1_p8), .Q(rs_ff_1_q));  // open: nQ
  Register #(.Bits(8)) register_1 (.D(d_ff_1_q), .C(clk), .en(rs_ff_as_1_q), .Q(register_1_q));
  // QTC qtc_1: pin names not known; wires that end beside it: Turn_On_out, clk, rs_ff_1_q, register_1_q, 1'b1, qtc_1_p6, qtc_1_p7, qtc_1_p8, qtc_1_p9
  LED led_1 (.in(qtc_1_p9));
  Register #(.Bits(8)) Out (.D(qtc_1_p7), .C(clk), .en(qtc_1_p6), .Q(Out_q));
  // Probe Output on Out_q

  // Notes on the sheet:
  //   clk: Hz: 8
endmodule
